// Digital circuit 32位计算机.dig as structural Verilog
module \_32位计算机  (
  input  Clock,
  output [31:0] out_2,
  output [31:0] out_3,
  output [3:0] out_4,
  output [7:0] out_5
);

  wire add_1_c_o, and_3_out, and_4_out, and_5_out, and_6_out, and_7_out, and_8_out, and_9_out, clock_t,
       CLR_IE, comparator_1_eq, comparator_2_eq, comparator_3_eq, comparator_4_eq, CS_IVT, CS_KeyBoard,
       CS_RAM, CS_ROM, CS_Stack, CS_Terminal, DN_SP, driverinvsel_1_out, END_CYCLE, Flag_c, Flag_z, HALT,
       INC_PC, INT_RET, INT_TAKE, keyboard_1_av, LD_IR, LD_MAR, LD_MDREXT, LD_MDRINT, LD_PC, LD_RFlags,
       LD_Rflags_Bus, LD_Rw, LD_SP, multiplexer_3_out, multiplexer_5_out, multiplexer_6_out,
       multiplexer_7_out, not_1_out, not_2_out, not_4_out, not_5_out, not_6_out, not_7_out, not_8_out,
       not_9_out, not_10_out, not_11_out, not_12_out, OE, OE_ALU, OE_INT_REQ, OE_MDREXT, OE_MDRINT, OE_PC,
       OE_Ra, OE_Rb, OE_Rflags, OE_SP, or_1_out, or_5_out, or_6_out, or_7_out, R_IE_q, SET_IE, sub_1_c_o,
       UP_SP, WE;
  wire [3:0] ADDR_Ra, ADDR_Rb, ADDR_Rw, MODE_ALU;
  wire [15:0] keyboard_1_d;
  wire [16:0] driver_9_out;
  wire [29:0] CU_d, multiplexer_1_out;
  wire [29:21] multiplexer_2_out;
  wire [31:0] add_1_s, and_2_out, barrelshifter_1_out, CU_INT_d, DEC_s, div_1_q, div_1_r, driver_1_out,
       INC_s, INT_REQ, MAR_q, MDR_EXT_q, MDR_INT_q, multiplexer_4_out, nand_1_out, nor_1_out, not_3_out,
       or_2_out, RegFile_da, RegFile_db, sub_1_s, xnor_1_out, xor_1_out;
  wire [31:17] driver_9_out_2;
  wire [31:20] IR_q;
  wire [63:0] mul_1_mul;

  CounterPreset #(.Bits(32), .isProgramCounter("true")) PC (
    .en(INC_PC), .C(clock_t), .dir(1'b0), .in(driver_1_out), .ld(LD_PC), .clr(1'b0), .out(out_2));  // open: ovf
  not not_1 (not_1_out, HALT);
  and and_1 (clock_t, Clock, not_1_out);
  assign driver_1_out = OE_PC ? out_2 : 32'bz;  // Driver driver_1
  CounterPreset #(.maxValue(15), .Bits(4)) STATE (
    .en(1'b1), .C(clock_t), .dir(1'b0), .in(4'b0000), .ld(1'b0), .clr(END_CYCLE), .out(out_4));  // open: ovf
  Register #(.Bits(32)) IR (.D(driver_1_out), .C(clock_t), .en(LD_IR), .Q({IR_q, ADDR_Ra, ADDR_Rb, ADDR_Rw, out_5}));
  assign driver_1_out = OE_Rflags ? {{30{1'b0}}, Flag_c, Flag_z} : 32'bz;  // Driver driver_2
  assign driver_1_out = OE_INT_REQ ? INT_REQ : 32'bz;  // Driver driver_3
  Comparator #(.Bits(8)) u_HALT (.a(out_5), .b(8'hf0), .eq(HALT));  // open: gt, lt
  assign driver_1_out = OE_Ra ? RegFile_da : 32'bz;  // Driver driver_4
  RegisterFile #(.AddrBits(4), .Bits(32)) RegFile (
    .Din(driver_1_out), .we(LD_Rw), .Rw(ADDR_Rw), .C(clock_t), .Ra(ADDR_Ra), .Rb(ADDR_Rb), .Da(RegFile_da),
    .Db(RegFile_db));
  assign driver_1_out = OE_Rb ? RegFile_db : 32'bz;  // Driver driver_5
  or or_1 (or_1_out, DN_SP, UP_SP);
  CounterPreset #(.Bits(32)) SP (
    .en(or_1_out), .C(clock_t), .dir(DN_SP), .in(driver_1_out), .ld(LD_SP), .clr(1'b0), .out(out_3));  // open: ovf
  assign driver_1_out = OE_SP ? out_3 : 32'bz;  // Driver driver_6
  ROM #(.AddrBits(4), .Bits(32)) CU_INT (.A(out_4), .sel(INT_TAKE), .D(CU_INT_d));
  not not_2 (not_2_out, INT_TAKE);
  assign driver_1_out = OE_ALU ? multiplexer_4_out : 32'bz;  // Driver driver_7
  Comparator #(.Bits(8)) comparator_1 (.a(out_5), .b(8'h33), .eq(comparator_1_eq));  // open: gt, lt
  Multiplexer #(.Bits(32)) multiplexer_1 (
    .sel(INT_TAKE), .in_0({32{1'b0}}), .in_1(CU_INT_d), .out({INT_RET, OE_INT_REQ, multiplexer_1_out}));
  ROM #(.AddrBits(12), .isProgramMemory("true"), .Bits(30)) CU (.A({out_5, out_4}), .sel(not_2_out), .D(CU_d));
  Add #(.Bits(32)) add_1 (.a(RegFile_da), .b(RegFile_db), .c_i(1'b0), .s(add_1_s), .c_o(add_1_c_o));
  Sub #(.Bits(32)) sub_1 (.a(RegFile_da), .b(RegFile_db), .c_i(1'b0), .s(sub_1_s), .c_o(sub_1_c_o));
  Mul #(.Bits(32)) mul_1 (.a(RegFile_da), .b(RegFile_db), .mul(mul_1_mul));
  Div #(.Bits(32)) div_1 (.a(RegFile_da), .b(RegFile_db), .q(div_1_q), .r(div_1_r));
  BarrelShifter #(.Bits(32)) barrelshifter_1 (.in(RegFile_da), .shift(RegFile_db[5:0]), .out(barrelshifter_1_out));
  assign and_2_out = RegFile_da & RegFile_db;  // And and_2, 32 bits wide
  assign nand_1_out = ~(RegFile_da & RegFile_db);  // NAnd nand_1, 32 bits wide
  assign or_2_out = RegFile_da | RegFile_db;  // Or or_2, 32 bits wide
  assign nor_1_out = ~(RegFile_da | RegFile_db);  // NOr nor_1, 32 bits wide
  assign xor_1_out = RegFile_da ^ RegFile_db;  // XOr xor_1, 32 bits wide
  assign xnor_1_out = ~(RegFile_da ^ RegFile_db);  // XNOr xnor_1, 32 bits wide
  assign not_3_out = ~RegFile_da;  // Not not_3, 32 bits wide
  Add #(.Bits(32)) INC (.a(RegFile_da), .b(32'h1), .c_i(1'b0), .s(INC_s));  // open: c_o
  Sub #(.Bits(32)) DEC (.a(RegFile_da), .b(32'h1), .c_i(1'b0), .s(DEC_s));  // open: c_o
  assign driverinvsel_1_out = ~comparator_1_eq ? and_4_out : 1'bz;  // DriverInvSel driverinvsel_1
  or or_3 (INC_PC, multiplexer_2_out[21], driverinvsel_1_out);
  Multiplexer #(.Bits(30)) multiplexer_2 (
    .sel(INT_TAKE), .in_0(CU_d), .in_1(multiplexer_1_out),
    .out({multiplexer_2_out[29:28], MODE_ALU, WE, OE, multiplexer_2_out[21], SET_IE, CLR_IE, OE_ALU, OE_Rflags, OE_Rb, OE_Ra, OE_MDREXT, OE_MDRINT, OE_PC, OE_SP, LD_Rflags_Bus, LD_RFlags, LD_Rw, LD_IR, LD_MDREXT, LD_MDRINT, LD_MAR, LD_PC, LD_SP, UP_SP, DN_SP}));
  or or_4 (END_CYCLE, and_4_out, multiplexer_2_out[29]);
  not not_4 (not_4_out, Flag_c);
  and and_3 (and_3_out, not_4_out, not_5_out);
  not not_5 (not_5_out, Flag_z);
  not not_6 (not_6_out, Flag_c);
  not not_7 (not_7_out, Flag_z);
  not not_8 (not_8_out, and_3_out);
  Multiplexer #(.Selector_Bits(4)) multiplexer_3 (
    .sel(IR_q[23:20]), .in_0(1'b0), .in_1(Flag_c), .in_2(Flag_z), .in_3(and_3_out), .in_4(not_6_out),
    .in_5(not_7_out), .in_6(not_8_out), .in_7(1'b0), .in_8(1'b0), .in_9(1'b0), .in_10(1'b0), .in_11(1'b0),
    .in_12(1'b0), .in_13(1'b0), .in_14(1'b0), .in_15(1'b0), .out(multiplexer_3_out));
  not not_9 (not_9_out, multiplexer_3_out);
  and and_4 (and_4_out, multiplexer_2_out[28], not_9_out);
  assign driver_1_out = OE_MDRINT ? MDR_INT_q : 32'bz;  // Driver driver_8
  Register #(.Bits(32)) MDR_EXT (.D(driver_1_out), .C(clock_t), .en(LD_MDREXT), .Q(MDR_EXT_q));
  Comparator #(.Bits(32)) comparator_2 (.a(INT_REQ), .b({32{1'b0}}), .eq(comparator_2_eq));  // open: gt, lt
  Register #(.Bits(32)) MDR_INT (.D({driver_9_out_2, driver_9_out}), .C(clock_t), .en(LD_MDRINT), .Q(MDR_INT_q));
  assign {driver_9_out_2, driver_9_out} = OE_MDREXT ? MDR_EXT_q : 32'bz;  // Driver driver_9
  and and_5 (and_5_out, multiplexer_2_out[29], not_10_out, R_IE_q);
  not not_10 (not_10_out, comparator_2_eq);
  RS_FF R_IE (.S(SET_IE), .C(clock_t), .R(CLR_IE), .Q(R_IE_q));  // open: nQ
  Multiplexer #(.Selector_Bits(4), .Bits(32)) multiplexer_4 (
    .sel(MODE_ALU), .in_0(add_1_s), .in_1(sub_1_s), .in_2(mul_1_mul[31:0]), .in_3(div_1_q),
    .in_4(barrelshifter_1_out), .in_5(and_2_out), .in_6(nand_1_out), .in_7(or_2_out), .in_8(nor_1_out),
    .in_9(xor_1_out), .in_10(xnor_1_out), .in_11(not_3_out), .in_12(INC_s), .in_13(DEC_s), .in_14(div_1_r),
    .in_15({32{1'b0}}), .out(multiplexer_4_out));
  Register #(.Bits(32)) MAR (.D(driver_1_out), .C(clock_t), .en(LD_MAR), .Q(MAR_q));
  RS_FF rs_ff_1 (.S(and_5_out), .C(clock_t), .R(INT_RET), .Q(INT_TAKE));  // open: nQ
  Comparator #(.Bits(32)) comparator_3 (.a({32{1'b0}}), .b(multiplexer_4_out), .eq(comparator_3_eq));  // open: gt, lt
  Multiplexer multiplexer_5 (.sel(comparator_4_eq), .in_0(add_1_c_o), .in_1(sub_1_c_o), .out(multiplexer_5_out));
  Comparator #(.Bits(4)) comparator_4 (.a(MODE_ALU), .b(4'b0001), .eq(comparator_4_eq));  // open: gt, lt
  Multiplexer multiplexer_6 (
    .sel(not_11_out), .in_0(driver_1_out[1]), .in_1(multiplexer_5_out), .out(multiplexer_6_out));
  not not_11 (not_11_out, LD_Rflags_Bus);
  not not_12 (not_12_out, LD_Rflags_Bus);
  Multiplexer multiplexer_7 (.sel(not_12_out), .in_0(driver_1_out[0]), .in_1(comparator_3_eq), .out(multiplexer_7_out));
  or or_5 (or_5_out, LD_Rflags_Bus, LD_RFlags);
  or or_6 (or_6_out, LD_Rflags_Bus, LD_RFlags);
  Decoder #(.Selector_Bits(4)) decoder_1 (
    .sel(MAR_q[27:24]), .out_0(CS_ROM), .out_1(CS_RAM), .out_2(CS_Stack), .out_3(CS_IVT),
    .out_4(CS_KeyBoard), .out_5(CS_Terminal));  // open: out_6, out_7, out_8, out_9, out_10, out_11, out_12, out_13, out_14, out_15
  Register register_1 (.D(multiplexer_7_out), .C(clock_t), .en(or_5_out), .Q(Flag_z));
  Register register_2 (.D(multiplexer_6_out), .C(clock_t), .en(or_6_out), .Q(Flag_c));
  and and_6 (and_6_out, CS_Terminal, WE);
  or or_7 (or_7_out, WE, OE);
  and and_7 (and_7_out, CS_KeyBoard, OE);
  EEPROM #(.AddrBits(24), .Bits(32)) ROM (
    .A(MAR_q[23:0]), .CS(CS_ROM), .WE(1'b0), .OE(OE), .D({driver_9_out_2, driver_9_out}));
  RAMSinglePortSel #(.AddrBits(24), .Bits(32)) RAM (
    .A(MAR_q[23:0]), .CS(CS_RAM), .WE(WE), .OE(OE), .D({driver_9_out_2, driver_9_out}));
  RAMSinglePortSel #(.AddrBits(24), .Bits(32)) Stack (
    .A(MAR_q[23:0]), .CS(CS_Stack), .WE(WE), .OE(OE), .D({driver_9_out_2, driver_9_out}));
  RAMSinglePortSel #(.AddrBits(24), .Bits(32)) IVT (
    .A(MAR_q[23:0]), .CS(and_8_out), .WE(WE), .OE(OE), .D({driver_9_out_2, driver_9_out}));
  and and_8 (and_8_out, CS_IVT, or_7_out);
  Keyboard keyboard_1 (.C(clock_t), .en(and_7_out), .D(keyboard_1_d), .av(keyboard_1_av));
  Terminal terminal_1 (.D(driver_9_out), .C(clock_t), .en(and_6_out));
  and and_9 (and_9_out, CS_KeyBoard, OE);
  assign {driver_9_out_2, driver_9_out} = and_9_out ? {{16{1'b0}}, keyboard_1_d} : 32'bz;  // Driver driver_10
  Multiplexer #(.Bits(32)) multiplexer_8 (.sel(keyboard_1_av), .in_0({32{1'b0}}), .in_1(32'h3000000), .out(INT_REQ));

  // Notes on the sheet:
  //   Clock: Hz: 65536
  //   contents of CU_INT (hex, n*v repeats v):
  //   f080810,f001040,f804002,f000810,f020040,f804002,4f000010,f400020,af002008
  //   ALU
  //   contents of CU (hex, n*v repeats v):
  //   f001010,f600020,f002080,2f000000,12*0,f001010,f600020,f002080
  //   ,2f000000,12*0,f001010,f600020,f002080,2f000000,12*0,f001010,f600020
  //   ,f002080,2f000000,12*0,f001010,f600020,f002080,2f000000,12*0,f001010
  //   ,f600020,f002080,2f000000,12*0,f001010,f600020,f002080,2f000000
  //   ,12*0,f001010,f600020,f002080,2f000000,12*0,f001010,f600020,f002080
  //   ,2f000000,12*0,f001010,f600020,f002080,2f000000,12*0,f001010,f600020
  //   ,f002080,2f000000,12*0,f001010,f600020,f002080,2f000000,12*0,f001010
  //   ,f600020,f002080,2f000000,12*0,f001010,f600020,f002080,2f000000
  //   ,12*0,f001010,f600020,f002080,2f000000,12*0,f001010,f600020,f002080
  //   ,2f000000,12*0,f001010,f600020,f002080,2f008100,12*0,f001010,f600020
  //   ,f002080,f010010,f400020,2f002100,10*0,f001010,f600020,f002080
  //   ,f010010,f008040,2f804000,10*0,f001010,f600020,f002080,f001010
  //   ,f600020,f002010,f400020,2f002100,8*0,f001010,f600020,f002080
  //   ,f001010,f600020,f002010,f008040,2f804000,8*0,f001010,f600020
  //   ,f002080,f201010,f400020,2f002100,10*0,f001010,f600020,f002080
  //   ,f201010,f400020,2f002100,10*0,f001010,f600020,f002080,40010,f400020
  //   ,2f002100,10*0,f001010,f600020,f002080,2f000000,12*0,f001010,f600020
  //   ,f002080,2f000000,12*0,f001010,f600020,f002080,2f000000,12*0,f001010
  //   ,f600020,f002080,2f000000,12*0,f001010,f600020,f002080,2f000000
  //   ,12*0,f001010,f600020,f002080,2f000000,12*0,f001010,f600020,f002080
  //   ,2f000000,12*0,f001010,f600020,f002080,2f000000,12*0,f001010,f600020
  //   ,f002080,20040300,12*0,f001010,f600020,f002080,21040300,12*0,f001010
  //   ,f600020,f002080,2c040100,12*0,f001010,f600020,f002080,2d040100
  //   ,12*0,f001010,f600020,f002080,22040300,12*0,f001010,f600020,f002080
  //   ,23040300,12*0,f001010,f600020,f002080,2e040300,12*0,f001010,f600020
  //   ,f002080,24040300,12*0,f001010,f600020,f002080,25040300,12*0,f001010
  //   ,f600020,f002080,26040300,12*0,f001010,f600020,f002080,27040300
  //   ,12*0,f001010,f600020,f002080,28040300,12*0,f001010,f600020,f002080
  //   ,29040300,12*0,f001010,f600020,f002080,2a040300,12*0,f001010,f600020
  //   ,f002080,2b040300,12*0,f001010,f600020,f002080,21040200,12*0,f001010
  //   ,f600020,f002080,f001010,f600020,2f002008,10*0,f001010,f600020
  //   ,f002080,10000000,f001010,f600020,2f002008,9*0,f001010,f600020
  //   ,f002080,2f008008,12*0,f001010,f600020,f002080,10000000,2f008008
  //   ,11*0,f001010,f600020,f002080,f201010,f400020,f000810,f001040
  //   ,f804002,2f002008,7*0,f001010,f600020,f002080,10000000,f201010
  //   ,f400020,f000810,f001040,f804002,2f002008,6*0,f001010,f600020
  //   ,f002080,f000001,f000810,f400020,2f002008,9*0,f001010,f600020
  //   ,f002080,f201010,f400020,f000810,f001040,f804002,f000810,f020040
  //   ,f804002,2f002008,4*0,f001010,f600020,f002080,10000000,f201010
  //   ,f400020,f000810,f001040,f804002,f000810,f020040,f804002,2f002008
  //   ,0,0,0,f001010,f600020,f002080,f100001,f000810,f400020,f002401
  //   ,f000810,f400020,2f002008,6*0,f001010,f600020,f002080,2f100000
  //   ,12*0,f001010,f600020,f002080,2f080000,12*0,f001010,f600020,f002080
  //   ,2f000000,12*0,f001010,f600020,f002080,2f000000,12*0,f001010,f600020
  //   ,f002080,2f000000,12*0,f001010,f600020,f002080,2f000000,12*0,f001010
  //   ,f600020,f002080,f000810,f008040,2f814002,10*0,f001010,f600020
  //   ,f002080,f000001,f000810,f400020,2f002100,9*0,f001010,f600020
  //   ,f002080,2f008004,12*0,f001010,f600020,f002080,2f000000,12*0,f001010
  //   ,f600020,f002080,2f000000,12*0,f001010,f600020,f002080,2f000000
  //   ,12*0,f001010,f600020,f002080,2f000000,12*0,f001010,f600020,f002080
  //   ,2f000000,12*0,f001010,f600020,f002080,2f000000,12*0,f001010,f600020
  //   ,f002080,2f000000,12*0,f001010,f600020,f002080,2f000000,12*0,f001010
  //   ,f600020,f002080,2f000000,12*0,f001010,f600020,f002080,2f000000
  //   ,12*0,f001010,f600020,f002080,2f000000,12*0,f001010,f600020,f002080
  //   ,2f000000,12*0,f001010,f600020,f002080,2f000000,12*0,f001010,f600020
  //   ,f002080,2f000000,12*0,f001010,f600020,f002080,2f000000,12*0,f001010
  //   ,f600020,f002080,2f000000,12*0,f001010,f600020,f002080,2f000000
  //   ,12*0,f001010,f600020,f002080,2f000000,12*0,f001010,f600020,f002080
  //   ,2f000000,12*0,f001010,f600020,f002080,2f000000,12*0,f001010,f600020
  //   ,f002080,2f000000,12*0,f001010,f600020,f002080,2f000000,12*0,f001010
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  //   contents of ROM (hex, n*v repeats v):
  //   915,8f5a371c,90014,1000000,915,a63f778e,90014,1000001,915,7349bc73
  //   ,90014,1000002,915,13131313,90014,1000003,915,99346fbc,90014,1000004
  //   ,f16,2000000,f0042,a16,1000000,b16,1000004,30,1d,a011,a0a22,a111
  //   ,1002f,100035,28,ab02f,200035,2e,30,1d,a012,a0a23,1a012,a0a22
  //   ,c0c22,36,cd02f,200031,36,a16,1000000,c15,0,36,f0
endmodule
